# Fritzing sketch LED blinking (saved by Fritzing 0.9.2b)
breadboards: 2

parts:
  ARM_1 = Explore Cortex M3 LPC1768 [chip_label=IC package="DIP (Dual Inline) [THT]"]
  R1 = Resistor [tolerance=±5% resistance=220 package=THT]
  LED1 = LED - 5mm [color="Red (633nm)" package="5 mm [THT]"]

nets:
  N1: ARM_1.pin2, R1.Pin_0
  N2: ARM_1.pin_40, LED1.anode
  N3: R1.Pin_1, LED1.cathode
